# Fritzing sketch draft (saved by Fritzing 0.8.7b)

parts:
  Componente1 = Arduino Uno (Rev3)  # not connected
  Componente2 = Arduino Prototyping Shield
  RF_Receiver1 = RF_Receiver
  RF_Sender_433_Mhz1 = RF Sender
  LED1 = LED - 5mm [color="Red (633nm)" package="5 mm [THT]"]
  LED3 = LED - 5mm [color="Yellow (595nm)" package="5 mm [THT]"]
  LED4 = LED - 5mm [color="Infrared (940nm)" package="5 mm [THT]"]
  LED5 = LED - 5mm [color="Infrared (940nm)" package="5 mm [THT]"]
  LED2 = LED - 5mm [color="Green (555nm)" package="5 mm [THT]"]
  R1 = Resistor [tolerance=±5% resistance=82 package=THT]
  NPN_Transistor1 = NPN-Transistor [package="TO92 [THT]"]
  IR1 = TSOP312.., 314.. [package=THT]
  R3 = Resistor [tolerance=±5% resistance=82 package=THT]
  R4 = Resistor [tolerance=±5% resistance=33k package=THT]
  R5 = Resistor [tolerance=±5% resistance=82 package=THT]
  R6 = Resistor [tolerance=±5% resistance=270 package=THT]
  Componente3 = Arduino Prototyping Shield
  R8 = Resistor [tolerance=±5% resistance=150 package=THT]
  R10 = Resistor [tolerance=±5% resistance=270 package=THT]
  NPN_Transistor2 = NPN-Transistor [package="TO92 [THT]"]  # not connected
  R11 = Resistor [tolerance=±5% resistance=39 package=THT]
  RF_Receiver2 = RF_Receiver
  LED6 = LED - 5mm [color="Yellow (595nm)" package="5 mm [THT]"]
  LED7 = LED - 5mm [color="Red (633nm)" package="5 mm [THT]"]
  LED8 = LED - 5mm [color="Green (555nm)" package="5 mm [THT]"]
  LED9 = LED - 5mm [color="Infrared (940nm)" package="5 mm [THT]"]
  LED10 = LED - 5mm [color="Infrared (940nm)" package="5 mm [THT]"]
  IR2 = TSOP312.., 314.. [package=THT]
  R12 = Resistor [tolerance=±5% resistance=100 package=THT]
  NPN_Transistor4 = NPN-Transistor [package="TO92 [THT]"]
  R14 = Resistor [tolerance=±5% resistance=150 package=THT]

nets:
  GND: Componente2.GND, Componente2.N$203, Componente2.N$235, Componente2.N$362, Componente2.N$367, Componente2.N$371, RF_Receiver1.GND, LED1.cathode, LED3.cathode, LED2.cathode, NPN_Transistor1.E, IR1.GND
  N1: Componente2.D8, Componente2.N$411, R5.Pin_1
  N2: Componente2.D9, Componente2.N$310, R4.Pin_1
  N3: Componente2.D1(TX), IR1.Data
  N4: Componente2.D2, RF_Receiver1.DIN
  N5: Componente2.D3, Componente2.N$38, R3.Pin_1
  N6: Componente2.D5, Componente2.N$305
  N7: Componente2.D7, Componente2.N$413, R1.Pin_1
  +5V: Componente2.+5V, Componente2.N$48, Componente2.N$281, Componente2.N$315, Componente2.N$360, RF_Receiver1.VIN, IR1.Vs
  N8: Componente2.+9V, Componente2.N$356, R6.Pin_1
  N9: Componente2.N$369, LED4.cathode, LED5.cathode, NPN_Transistor1.C
  N10: Componente2.N$370, Componente2.N$379, NPN_Transistor1.B, R3.Pin_0
  N11: Componente2.N$399, LED2.anode, R4.Pin_0
  N12: Componente2.N$402, LED1.anode, R5.Pin_0
  N13: Componente2.N$405, LED3.anode
  N14: Componente2.N$406, R1.Pin_0
  GND_2: RF_Sender_433_Mhz1.GND, Componente3.GND, Componente3.N$77, Componente3.N$118, Componente3.N$251, Componente3.N$353, RF_Receiver2.GND, LED6.cathode, LED7.cathode, LED8.cathode, IR2.GND, NPN_Transistor4.E
  N15: RF_Sender_433_Mhz1.DIN, Componente3.D6, Componente3.N$305
  VIN: RF_Sender_433_Mhz1.VIN, Componente3.+5V, Componente3.N$273, Componente3.N$283, Componente3.N$292, Componente3.N$368, R11.Pin_1, RF_Receiver2.VIN, IR2.Vs
  N16: LED4.anode, LED5.anode, R6.Pin_0
  N17: Componente3.D9, Componente3.N$168, R12.Pin_1
  N18: Componente3.D1(TX), IR2.Data
  N19: Componente3.D2, RF_Receiver2.DIN
  N20: Componente3.D3, R10.Pin_1
  N21: Componente3.D4, R8.Pin_1
  N22: Componente3.D5, R14.Pin_1
  N23: Componente3.N$94, LED9.cathode, LED10.cathode, NPN_Transistor4.C
  N24: Componente3.N$95, NPN_Transistor4.B
  N25: Componente3.N$120, R12.Pin_0
  N26: Componente3.N$365, R11.Pin_0, LED9.anode, LED10.anode
  N27: Componente3.N$407, R10.Pin_0, LED6.anode
  N28: Componente3.N$409, R8.Pin_0, LED7.anode
  N29: Componente3.N$412, LED8.anode, R14.Pin_0

custom parts:
  TSOP312.., 314..: The TSOP312.., TSOP314.. series are miniaturized receivers for infrared remote control systems. A PIN diode and a preamplifier are assembled on a lead frame, the epoxy package acts as an IR filter. The demodulated output signal can be directly decoded by a microprocessor. The TSOP312.. is compatible with all common IR remote control data formats. The TSOP314.. is optimized to suppress almost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
